# Fritzing sketch circuit (saved by Fritzing 0.9.9b)

parts:
  Part1 = Arduino Nano (Rev3.0)
  Part2 = Motor Driver 1A Dual TB6612FNG
  Part3 = Bluetooth HC-05 Macho
  M1 = DC Motor
  M2 = DC Motor
  M3 = DC Motor
  M4 = DC Motor
  Power_plug1 = Power plug

nets:
  N1: Part1.D3, Part2.AIN1
  N2: Part1.D4, Part2.AIN2
  N3: Part1.D5, Part2.PWMA
  N4: Part1.D6, Part2.PWMB
  N5: Part1.D7, Part3.RXD
  N6: Part1.D8, Part3.TXD
  N7: Part1.D9, Part2.BIN2
  N8: Part1.D10, Part2.BIN1
  VIN: Part1.VIN, Part2.VM, Power_plug1.VCC
  GND: Part1.GND, Part2.GND, Part3.GND, Power_plug1.GND
  VCC: Part1.5V, Part2.VCC, Part2.STBY, Part3.VCC
  N9: Part2.B01, M1.pin_2, M3.pin_1
  N10: Part2.B02, M1.pin_1, M3.pin_2
  N11: Part2.A02, M2.pin_1, M4.pin_2
  N12: Part2.A01, M2.pin_2, M4.pin_1
