# Fritzing sketch diagram (saved by Fritzing 0.9.9b)

parts:
  Part1 = Arduino Nano (Rev3.0)
  Part2 = Bluetooth HC-05 Macho

nets:
  N1: Part1.D7, Part2.TXD
  N2: Part1.D8, Part2.RXD
  GND: Part1.GND, Part2.GND
  5V: Part1.5V, Part2.VCC
